# Fritzing sketch sketch (saved by Fritzing 0.9.2b)
breadboards: 1

parts:
  R1 = Resistor [tolerance=±5% resistance=120 package=THT]
  R2 = Resistor [tolerance=±5% resistance=120 package="0805 [SMD]"]
  R3 = Resistor [tolerance=±5% resistance=120 package="0805 [SMD]"]
  R4 = Resistor [tolerance=±5% resistance=500 package="0805 [SMD]"]
  R5 = Resistor [tolerance=±5% resistance=500 package="0805 [SMD]"]
  R6 = Resistor [tolerance=±5% resistance=120 package="0805 [SMD]"]
  R7 = Rotary Potentiometer (Large) [maximum_resistance=100kΩ package=THT]
  Part1 = Arduino Uno (Rev3) - ICSP
  J1 = Piezo Speaker
  J2 = Piezo Speaker
  Part2 = Bluetooth HC-05 Macho
  Part3 = Logic Level Converter
  R8 = Resistor [tolerance=±5% resistance=2.2k part_number=TV package="0805 [SMD]"]

nets (from the schematic view):
  N1: R1.Pin_0, R6.Pin_1
  N2: R1.Pin_1, R2.Pin_0
  N3: R2.Pin_1, R3.Pin_1
  N4: R3.Pin_0, Part1.D7
  N5: R4.Pin_0, R5.Pin_1
  N6: R4.Pin_1, R6.Pin_0, R8.Pin_1
  N7: R5.Pin_0, Part1.D9_PWM
  N8: R7.leg1, Part1.GND, J1.pin1, J2.pin1, Part3.RX2_LV, R8.Pin_0
  N9: R7.wiper, Part1.A0
  5V: R7.leg2, Part1.5V, Part2.VCC
  N10: Part1.D10_PWM/SS, J1.pin2
  N11: Part1.D11_PWM/MOSI, J2.pin2
  N12: Part2.GND, Part3.RX2_HV

notes:
  TV
  Arduino
  TV out circuit
  Buzzers
  Bluetooth HC-05
  Logic converter
  Joystick

custom parts:
  Logic Level Converter: Description: If you've ever tried to connect a 3.3V device to a 5V system, you know what a challenge it can be. The SparkFun logic level converter is a small device that safely steps down 5V signals to 3.3V and steps up 3.3V to 5V. This level converter also works with 2.8V and 1.8V devices. Each level converter has the capability of converting 4 pins on the high side to 4 pins on the low side.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
